# Fritzing sketch sketch (saved by Fritzing 0.9.3b)
breadboards: 1

parts:
  U1 = ESP8266 NodeMCU LoLin base
  ZS-042_RTC1 = ZS-042 RTC Module
  SERVO1 = Tower Pro SG90 servo [part_number=101246]
  Part1 = Ambient Light Sensor (TEMT6000 Breakout Board)
  S1 = Momentary Switch [package=ksa_sealed_tac_switch]
  R1 = Resistor [tolerance=±5% resistance=10k package=THT]
  LED1 = LED - 5mm [color="Red (633nm)" package="5 mm [THT]"]
  LED2 = LED - 5mm [color="Blue (430nm)" package="5 mm [THT]"]
  R2 = Resistor [tolerance=±5% resistance=330 package=THT]
  R3 = Resistor [tolerance=±5% resistance=330 package=THT]

nets:
  GND: U1.GND1-0, U1.GND3-0, U1.GND3-2, U1.GND3-3, U1.GND8-4, U1.GND8-10, ZS-042_RTC1.GND, SERVO1.GND, Part1.GND, R1.Pin_1, R2.Pin_1, R3.Pin_1
  VCC: U1.3V1-0, U1.3V1-1, U1.3V3-0, U1.3V3-2, ZS-042_RTC1.VCC, SERVO1.+5V, Part1.VCC
  N1: U1.D1-0, U1.D1-3, ZS-042_RTC1.SCL
  N2: U1.D2-0, U1.D2-3, ZS-042_RTC1.SDA
  N3: U1.D5-1, U1.D5-3, LED2.anode
  N4: U1.D6-0, U1.D6-2, LED1.anode
  N5: U1.D7-0, U1.D7-2, S1.3
  N6: U1.D8-2, U1.D8-3, SERVO1.Signal
  N7: LED1.cathode, R3.Pin_0
  N8: LED2.cathode, R2.Pin_0

custom parts:
  ESP8266 NodeMCU LoLin base: ESP8266 based NodeMCU Base
  Tower Pro SG90 servo: Original file by John De Cristofaro http://www.adafruit.com/products/1449 Adafruit Feedback Servo (Small) Edited by: e-radionica.com 28/9/2015
